# Fritzing sketch arduino_plant_water_sensor (saved by Fritzing 0.8.7b)
breadboards: 1

parts:
  Water_Level_Sensor1 = Water Level Sensor
  LED3 = LED - 5mm [color="Green (555nm)" package="5 mm [THT]"]
  LED1 = LED - 5mm [color="Red (633nm)" package="5 mm [THT]"]
  LED2 = LED - 5mm [color="Orange (620nm)" package="5 mm [THT]"]
  Onderdeel1 = Arduino Nano (Rev3.0)
  R1 = Resistor [tolerance=±5% resistance=220 package=THT]
  R2 = Resistor [tolerance=±5% resistance=220 package=THT]
  R3 = Resistor [tolerance=±5% resistance=220 package=THT]

nets:
  N1: Water_Level_Sensor1.SIG, Onderdeel1.A0
  VCC: Water_Level_Sensor1.VCC, Onderdeel1.5V
  GND: Water_Level_Sensor1.GND, LED3.cathode, LED1.cathode, LED2.cathode, Onderdeel1.GND
  N2: LED3.anode, R1.Pin_0
  N3: LED1.anode, R3.Pin_0
  N4: LED2.anode, R2.Pin_0
  N5: Onderdeel1.D10, R3.Pin_1
  N6: Onderdeel1.D11/MOSI, R2.Pin_1
  N7: Onderdeel1.D12/MISO, R1.Pin_1

custom parts:
  Water Level Sensor: A water level sensor. This sensor operates at 3V to 5V. The Sig (signal) pin outputs an analogue signal that is in proportion to the amount of water in contact with the sensor.
